// Logisim project FISCSIM.circ as structural Verilog: 1 circuit, main circuit main
module main (
);

  wire and_1_out, B_out, clk, decoder_1_out0, decoder_1_out1, decoder_1_out2, decoder_1_out3, nor_1_out,
       not_1_out, not_2_out, register_2_q;
  wire [5:0] adder_1_out, multiplexer_1_out, register_1_q, rom_1_data;
  wire [7:0] adder_2_out, and_2_out, multiplexer_2_out, multiplexer_3_out, multiplexer_4_out, not_3_out,
       register_3_q, register_4_q, register_5_q, register_6_q;
  wire [7:6] rom_1_data_2;

  Multiplexer #(.width(6)) multiplexer_1 (
    .in0(adder_1_out), .in1(rom_1_data), .out(multiplexer_1_out), .sel(and_1_out));
  Register #(.width(6)) register_1 (.D(multiplexer_1_out), .clk(clk), .Q(register_1_q));  // open: en, clr
  ROM #(.addrWidth(6)) rom_1 (.addr(register_1_q), .data({rom_1_data_2, rom_1_data}));
  Adder #(.width(6)) adder_1 (.a(register_1_q), .b(6'b000001), .out(adder_1_out));  // open: cin, cout
  and and_1 (and_1_out, B_out, not_1_out);
  not not_1 (not_1_out, register_2_q);
  and B (B_out, rom_1_data_2[6], rom_1_data_2[7]);
  not not_2 (not_2_out, B_out);
  Decoder #(.select(2)) decoder_1 (
    .out0(decoder_1_out0), .out1(decoder_1_out1), .out2(decoder_1_out2), .out3(decoder_1_out3),
    .sel(rom_1_data[1:0]), .en(not_2_out));
  Register #(.width(1)) register_2 (.D(nor_1_out), .en(not_2_out), .clk(clk), .Q(register_2_q));  // open: clr
  Register #(.trigger("high")) register_3 (
    .D(multiplexer_4_out), .en(decoder_1_out0), .clk(clk), .Q(register_3_q));  // open: clr
  Register register_4 (.D(multiplexer_4_out), .en(decoder_1_out1), .clk(clk), .Q(register_4_q));  // open: clr
  Register register_5 (.D(multiplexer_4_out), .en(decoder_1_out2), .clk(clk), .Q(register_5_q));  // open: clr
  Register register_6 (.D(multiplexer_4_out), .en(decoder_1_out3), .clk(clk), .Q(register_6_q));  // open: clr
  Clock clock_1 (.out(clk));
  Hex_Digit_Display hex_digit_display_1 (.value(register_6_q[7:4]));  // open: dp
  nor nor_1 (nor_1_out, multiplexer_4_out[0], multiplexer_4_out[1], multiplexer_4_out[2], multiplexer_4_out[3], multiplexer_4_out[4], multiplexer_4_out[5], multiplexer_4_out[6], multiplexer_4_out[7]);
  Multiplexer #(.select(2), .width(8)) multiplexer_2 (
    .in0(register_3_q), .in1(register_4_q), .in2(register_5_q), .in3(register_6_q), .out(multiplexer_2_out),
    .sel(rom_1_data[5:4]));
  Multiplexer #(.select(2), .width(8)) multiplexer_3 (
    .in0(register_3_q), .in1(register_4_q), .in2(register_5_q), .in3(register_6_q), .out(multiplexer_3_out),
    .sel(rom_1_data[3:2]));
  Hex_Digit_Display hex_digit_display_2 (.value(register_6_q[3:0]));  // open: dp
  Adder adder_2 (.a(multiplexer_2_out), .b(multiplexer_3_out), .out(adder_2_out));  // open: cin, cout
  assign and_2_out = multiplexer_2_out & multiplexer_3_out;  // AND_Gate and_2, 8 bits wide
  assign not_3_out = ~multiplexer_2_out;  // NOT_Gate not_3, 8 bits wide
  Multiplexer #(.enable("true"), .select(2), .width(8)) multiplexer_4 (
    .in0(adder_2_out), .in1(and_2_out), .in2(not_3_out), .in3(not_3_out), .out(multiplexer_4_out),
    .sel(rom_1_data_2), .en(not_2_out));

  // Notes on the sheet:
  //   contents of rom_1 (hex, n*v repeats v):
  //   90 44 81 15 91 16 1a 2a 2a 2a 3 7c 7 7d 7 3a cb 55 d2
endmodule
