// Logisim project miscsim.circ as structural Verilog: 6 circuits, main circuit main
module main (
);

  wire alu_1_c, alu_1_z, clk, controller_1_alu_z_en, controller_1_c_en, controller_1_wd_en,
       controller_1_wr_en, decoder_1_out0, decoder_1_out1, displaydecoder_1_sign, displaydecoder_2_sign,
       F0_F1_out, F_out, multiplexer_2_out, not_1_out;
  wire [1:0] controller_1_wr_s, z_q;
  wire [3:0] controller_1_op, displaydecoder_1_hun, displaydecoder_1_one, displaydecoder_1_ten,
       displaydecoder_2_hun, displaydecoder_2_one, displaydecoder_2_ten;
  wire [7:0] alu_1_alu_output, F0_q, F1_q, multiplexer_1_out, ram_1_dout, registerfile_1_rda,
       registerfile_1_rdb, registerfile_1_rdc;
  wire [11:0] rom_1_data;
  wire [12:0] controller_1_pc_o, PC_q;

  ROM #(.addrWidth(13), .dataWidth(12)) rom_1 (.addr(PC_q), .data(rom_1_data));
  Register #(.width(13)) PC (.D(controller_1_pc_o), .clk(clk), .Q(PC_q));  // open: en, clr
  Multiplexer #(.enable("true"), .select(2), .width(8)) multiplexer_1 (
    .in0(alu_1_alu_output), .in1(registerfile_1_rda), .in2(ram_1_dout), .in3(rom_1_data[9:2]),
    .out(multiplexer_1_out), .sel(controller_1_wr_s), .en(controller_1_wr_en));
  Controller controller_1 (
    .status(z_q), .pc_i(PC_q), .word(rom_1_data), .pc_o(controller_1_pc_o), .wd_en(controller_1_wd_en),
    .c_en(controller_1_c_en), .op(controller_1_op), .alu_z_en(controller_1_alu_z_en), .clk_o(clk),
    .wr_s(controller_1_wr_s), .wr_en(controller_1_wr_en));
  RegisterFile registerfile_1 (
    .clk(clk), .we(controller_1_wr_en), .RAa(rom_1_data[5:4]), .RAb(rom_1_data[3:2]), .WAn(rom_1_data[1:0]),
    .WDn(multiplexer_1_out), .RDa(registerfile_1_rda), .RDb(registerfile_1_rdb), .RDc(registerfile_1_rdc));
  DisplayDecoder displaydecoder_1 (
    .bin(F0_q), .sign(displaydecoder_1_sign), .hun(displaydecoder_1_hun), .ten(displaydecoder_1_ten),
    .one(displaydecoder_1_one));
  DisplayDecoder displaydecoder_2 (
    .bin(F1_q), .sign(displaydecoder_2_sign), .hun(displaydecoder_2_hun), .ten(displaydecoder_2_ten),
    .one(displaydecoder_2_one));
  Register #(.width(1)) c (.D(alu_1_c), .en(controller_1_c_en), .clk(clk), .Q(z_q[1]));  // open: clr
  _7_Segment_Display u_7_segment_display_1 (.g(displaydecoder_1_sign));  // open: f, a, b, e, d, c, dp
  // _7_Segment_Display 7_segment_display_2: pin names not known; wires that end beside it: displaydecoder_1_hun, displaydecoder_1_ten
  // BCD_to_7_Segment_decoder bcd_to_7_segment_decoder_1: pin names not known
  _7_Segment_Display u_7_segment_display_3 (.g(displaydecoder_2_sign));  // open: f, a, b, e, d, c, dp
  // _7_Segment_Display 7_segment_display_4: pin names not known; wires that end beside it: displaydecoder_2_hun, displaydecoder_2_ten
  // BCD_to_7_Segment_decoder bcd_to_7_segment_decoder_2: pin names not known
  Register #(.width(1)) z (.D(alu_1_z), .en(controller_1_alu_z_en), .clk(clk), .Q(z_q[0]));  // open: clr
  // _7_Segment_Display 7_segment_display_5: pin names not known; wires that end beside it: displaydecoder_1_ten, displaydecoder_1_one
  _7_Segment_Display u_7_segment_display_6 ();  // open: g, f, a, b, e, d, c, dp
  // BCD_to_7_Segment_decoder bcd_to_7_segment_decoder_3: pin names not known
  // BCD_to_7_Segment_decoder bcd_to_7_segment_decoder_4: pin names not known
  // _7_Segment_Display 7_segment_display_7: pin names not known; wires that end beside it: displaydecoder_2_ten, displaydecoder_2_one
  _7_Segment_Display u_7_segment_display_8 ();  // open: g, f, a, b, e, d, c, dp
  // BCD_to_7_Segment_decoder bcd_to_7_segment_decoder_5: pin names not known
  // BCD_to_7_Segment_decoder bcd_to_7_segment_decoder_6: pin names not known
  and F (F_out, registerfile_1_rda[4], registerfile_1_rda[5], registerfile_1_rda[6], registerfile_1_rda[7], controller_1_wd_en);
  RAM #(.asyncread("true")) ram_1 (
    .addr(registerfile_1_rda), .we(multiplexer_2_out), .oe(1'b1), .clk(clk), .din(registerfile_1_rdc),
    .dout(ram_1_dout));
  Multiplexer multiplexer_2 (.in0(controller_1_wd_en), .in1(not_1_out), .out(multiplexer_2_out), .sel(F_out));
  not not_1 (not_1_out, controller_1_wd_en);
  ALU alu_1 (
    .c_sub_en(controller_1_c_en), .op(controller_1_op), .alu_en(controller_1_alu_z_en),
    .Rn(registerfile_1_rda), .Rm(registerfile_1_rdb), .Rd(registerfile_1_rdc), .c(alu_1_c), .z(alu_1_z),
    .ALU_output(alu_1_alu_output));
  _7_Segment_Display u_7_segment_display_9 (.g(1'b1), .f(1'b1), .a(1'b1), .e(1'b1));  // open: b, d, c, dp
  _7_Segment_Display u_7_segment_display_10 (.f(1'b1), .a(1'b1), .e(1'b1), .d(1'b1));  // open: g, b, c, dp
  and F0_F1 (F0_F1_out, ~registerfile_1_rda[1], ~registerfile_1_rda[2], ~registerfile_1_rda[3], F_out);  // AND_Gate
  Decoder decoder_1 (.out0(decoder_1_out0), .out1(decoder_1_out1), .sel(registerfile_1_rda[0]), .en(F0_F1_out));
  Register F0 (.D(registerfile_1_rdc), .en(decoder_1_out0), .clk(clk), .Q(F0_q));  // open: clr
  Register F1 (.D(registerfile_1_rdc), .en(decoder_1_out1), .clk(clk), .Q(F1_q));  // open: clr

  // Notes on the sheet:
  //   contents of rom_1 (hex, n*v repeats v):
  //   fbf c02 c05 fc0 302 26 302 26 fc4 303 37 fc0 302 26 302 26 fc4 303 37 fc0 302 26 302 26 fc4 303 37
  //   fc0 302 26 fc4 303 37 fc0 302 26 302 26 fc4 303 37 121 df8 90 c05 7d5 fc0 302 26 302 fc4 122 ea3 303
  //   aa 7cb bf 7c7
endmodule

module Controller (
  input  [1:0] status,
  input  [12:0] pc_i,
  input  [11:0] word,
  output [12:0] pc_o,
  output wd_en,
  output c_en,
  output [3:0] op,
  output alu_z_en,
  output clk_o,
  output [1:0] wr_s,
  output wr_en
);

  wire and_4_out, and_5_out, B_out, bcs_out, bnz_out, not_1_out, not_2_out, not_3_out, not_4_out, not_5_out,
       not_6_out, wrs0_out, wrs1_out, xor_1_out, xor_2_out;
  wire [12:0] bit_extender_1_out, multiplexer_1_out;

  assign bit_extender_1_out = {{3{word[9]}}, word[9:0]};  // Bit_Extender bit_extender_1
  not not_1 (not_1_out, word[11]);
  not not_2 (not_2_out, word[10]);
  not not_3 (not_3_out, word[9]);
  not not_4 (not_4_out, word[8]);
  not not_5 (not_5_out, word[7]);
  not not_6 (not_6_out, word[6]);
  Multiplexer #(.width(13)) multiplexer_1 (.in0(13'h1), .in1(bit_extender_1_out), .out(multiplexer_1_out), .sel(B_out));
  or B (B_out, bnz_out, bcs_out);
  and bnz (bnz_out, ~status[0], word[10], xor_1_out);  // AND_Gate
  and bcs (bcs_out, xor_1_out, word[11], status[1]);
  xor xor_1 (xor_1_out, word[10], word[11]);
  and and_1 (wd_en, not_6_out, not_5_out, word[8], word[9], not_2_out, not_1_out);
  and and_2 (c_en, not_5_out, not_4_out, not_3_out, not_2_out, not_1_out);
  and and_3 (alu_z_en, not_3_out, not_2_out, not_1_out);
  xor xor_2 (xor_2_out, word[10], word[11]);
  and and_4 (and_4_out, not_6_out, not_2_out, not_1_out, word[8], word[9]);
  and wrs1 (wrs1_out, not_5_out, word[8], word[9], not_2_out, not_1_out, word[6]);
  and and_5 (and_5_out, word[10], word[11]);
  and wrs0 (wrs0_out, not_4_out, not_2_out, not_1_out, word[9]);
  Adder #(.width(13)) adder_1 (.a(multiplexer_1_out), .b(pc_i), .out(pc_o));  // open: cin, cout
  Clock clock_1 (.out(clk_o));
  nor nor_1 (wr_en, xor_2_out, and_4_out);
  or or_1 (wr_s[1], wrs1_out, and_5_out);
  or or_2 (wr_s[0], and_5_out, wrs0_out);

  assign op = word[9:6];
endmodule

module ALU (
  input  c_sub_en,
  input  [3:0] op,
  input  alu_en,
  input  [7:0] Rn,
  input  [7:0] Rm,
  input  [7:0] Rd,
  output c,
  output z,
  output [7:0] ALU_output
);

  wire and_1_out, cla_2_c_out, sub_out;
  wire [3:0] cla_1_sum, cla_2_sum;
  wire [7:0] and_2_out, bit_extender_1_out, multiplexer_1_out, not_1_out, not_2_out, or_1_out;

  and and_1 (and_1_out, alu_en, ~op[3]);  // AND_Gate
  and sub (sub_out, op[0], c_sub_en);
  Multiplexer #(.width(8)) multiplexer_1 (.in0(Rm), .in1(not_1_out), .out(multiplexer_1_out), .sel(sub_out));
  assign not_1_out = ~Rm;  // NOT_Gate not_1, 8 bits wide
  CLA cla_1 (.C_in(cla_2_c_out), .A(Rn[7:4]), .B(multiplexer_1_out[7:4]), .C_out(c), .sum(cla_1_sum));
  CLA cla_2 (.C_in(sub_out), .A(Rn[3:0]), .B(multiplexer_1_out[3:0]), .C_out(cla_2_c_out), .sum(cla_2_sum));
  assign and_2_out = Rm & Rn;  // AND_Gate and_2, 8 bits wide
  assign or_1_out = Rm | Rn;  // OR_Gate or_1, 8 bits wide
  assign not_2_out = ~Rn;  // NOT_Gate not_2, 8 bits wide
  Multiplexer #(.enable("true"), .select(3), .width(8)) multiplexer_2 (
    .in0({cla_1_sum, cla_2_sum}), .in1({cla_1_sum, cla_2_sum}), .in2(and_2_out), .in3(or_1_out),
    .in4(not_2_out), .in5({Rd[6:0], 1'b0}), .in6(bit_extender_1_out), .in7(bit_extender_1_out),
    .out(ALU_output), .sel(op[2:0]), .en(and_1_out));
  assign bit_extender_1_out = {{1{Rd[7]}}, Rd[7:1]};  // Bit_Extender bit_extender_1
  nor nor_1 (z, ALU_output[0], ALU_output[1], ALU_output[2], ALU_output[3], ALU_output[4], ALU_output[5], ALU_output[6], ALU_output[7]);
endmodule

module RegisterFile (
  input  clk,
  input  we,
  input  [1:0] RAa,
  input  [1:0] RAb,
  input  [1:0] WAn,
  input  [7:0] WDn,
  output [7:0] RDa,
  output [7:0] RDb,
  output [7:0] RDc
);

  wire decoder_1_out0, decoder_1_out1, decoder_1_out2, decoder_1_out3;
  wire [7:0] register_1_q, register_2_q, register_3_q, register_4_q;

  Decoder #(.select(2)) decoder_1 (
    .out0(decoder_1_out0), .out1(decoder_1_out1), .out2(decoder_1_out2), .out3(decoder_1_out3), .sel(WAn),
    .en(we));
  Register register_1 (.D(WDn), .en(decoder_1_out0), .clk(clk), .Q(register_1_q));  // open: clr
  Register register_2 (.D(WDn), .en(decoder_1_out1), .clk(clk), .Q(register_2_q));  // open: clr
  Register register_3 (.D(WDn), .en(decoder_1_out2), .clk(clk), .Q(register_3_q));  // open: clr
  Register register_4 (.D(WDn), .en(decoder_1_out3), .clk(clk), .Q(register_4_q));  // open: clr
  Multiplexer #(.select(2), .width(8)) multiplexer_1 (
    .in0(register_1_q), .in1(register_2_q), .in2(register_3_q), .in3(register_4_q), .out(RDa), .sel(RAa));
  Multiplexer #(.select(2), .width(8)) multiplexer_2 (
    .in0(register_1_q), .in1(register_2_q), .in2(register_3_q), .in3(register_4_q), .out(RDb), .sel(RAb));
  Multiplexer #(.select(2), .width(8)) multiplexer_3 (
    .in0(register_1_q), .in1(register_2_q), .in2(register_3_q), .in3(register_4_q), .out(RDc), .sel(WAn));
endmodule

module CLA (
  input  C_in,
  input  [3:0] A,
  input  [3:0] B,
  output C_out,
  output [3:0] sum
);

  wire c0_out, c1_out, c2_out, g0_out, g1_out, g2_out, g3_out, p0_out, p0cin_out, p1_out, p1g0_out, p2_out,
       p2g1_out, p3_out, p3g2_out, p10cin_out, p21g0_out, p32g1_out, p210cin_out, p321g0_out, p3210cin_out,
       xor_1_out, xor_2_out, xor_3_out, xor_4_out;

  and p3210cin (p3210cin_out, C_in, p3_out, p2_out, p1_out, p0_out);
  and p321g0 (p321g0_out, p3_out, p2_out, p1_out, g0_out);
  or p3 (p3_out, B[3], A[3]);
  and p32g1 (p32g1_out, p3_out, p2_out, g1_out);
  and g3 (g3_out, B[3], A[3]);
  and p3g2 (p3g2_out, p3_out, g2_out);
  or c3 (C_out, p3210cin_out, p321g0_out, p32g1_out, p3g2_out, g3_out);
  and p210cin (p210cin_out, C_in, p2_out, p1_out, p0_out);
  and p21g0 (p21g0_out, p2_out, p1_out, g0_out);
  xor xor_1 (xor_1_out, B[3], A[3]);
  or p2 (p2_out, B[2], A[2]);
  and g2 (g2_out, B[2], A[2]);
  and p2g1 (p2g1_out, p2_out, g1_out);
  or c2 (c2_out, p210cin_out, p21g0_out, p2g1_out, g2_out);
  xor s3 (sum[3], xor_1_out, c2_out);
  or p1 (p1_out, B[1], A[1]);
  and p10cin (p10cin_out, C_in, p1_out, p0_out);
  xor xor_2 (xor_2_out, B[2], A[2]);
  and g1 (g1_out, B[1], A[1]);
  and p1g0 (p1g0_out, p1_out, g0_out);
  or c1 (c1_out, p10cin_out, p1g0_out, g1_out);
  xor s2 (sum[2], xor_2_out, c1_out);
  or p0 (p0_out, B[0], A[0]);
  and p0cin (p0cin_out, p0_out, C_in);
  or c0 (c0_out, p0cin_out, g0_out);
  xor xor_3 (xor_3_out, B[1], A[1]);
  xor s1 (sum[1], xor_3_out, c0_out);
  and g0 (g0_out, B[0], A[0]);
  xor xor_4 (xor_4_out, B[0], A[0]);
  xor s0 (sum[0], xor_4_out, C_in);
endmodule

module DisplayDecoder (
  input  [7:0] bin,
  output sign,
  output [3:0] hun,
  output [3:0] ten,
  output [3:0] one
);

  wire and_1_out, and_2_out, and_3_out, and_4_out, and_5_out, and_6_out, and_7_out, and_8_out, and_9_out,
       and_10_out, and_11_out, and_12_out, and_13_out, and_14_out, and_15_out, and_16_out, and_17_out,
       and_18_out, and_19_out, and_20_out, and_21_out, and_22_out, and_23_out, and_24_out, and_25_out,
       and_26_out, and_27_out, and_28_out, cla_2_c_out, not_2_out, not_3_out, not_4_out, not_5_out,
       not_6_out, not_7_out, not_8_out, or_1_out, or_2_out, or_3_out, or_4_out, or_5_out, or_6_out, or_7_out,
       or_8_out, or_9_out, or_10_out, or_11_out, or_12_out, or_13_out, or_14_out, xor_1_out, xor_2_out,
       xor_3_out, xor_4_out, xor_5_out, xor_6_out, xor_7_out, xor_8_out, xor_9_out, xor_10_out, xor_11_out,
       xor_12_out, xor_13_out, xor_14_out, xor_15_out, xor_16_out, xor_17_out, xor_18_out, xor_19_out,
       xor_21_out, xor_22_out, xor_23_out, xor_24_out, xor_25_out, xor_28_out, xor_29_out;
  wire [3:0] cla_1_sum;
  wire [3:1] cla_2_sum;
  wire [7:0] multiplexer_1_out, not_1_out;

  or or_1 (or_1_out, cla_1_sum[2], cla_1_sum[1]);
  or or_2 (or_2_out, 1'b0, and_1_out);
  and and_1 (and_1_out, cla_1_sum[3], or_1_out);
  Multiplexer #(.width(8)) multiplexer_1 (.in0(bin), .in1(not_1_out), .out(multiplexer_1_out), .sel(bin[7]));
  assign not_1_out = ~bin;  // NOT_Gate not_1, 8 bits wide
  xor xor_1 (xor_1_out, or_2_out, cla_1_sum[1]);
  not not_2 (not_2_out, cla_1_sum[2]);
  and and_2 (and_2_out, or_2_out, xor_1_out);
  xor xor_2 (xor_2_out, or_2_out, and_3_out);
  and and_3 (and_3_out, not_2_out, and_2_out);
  and and_4 (and_4_out, cla_1_sum[3], xor_2_out);
  xor xor_3 (xor_3_out, xor_2_out, cla_1_sum[3]);
  CLA cla_1 (.C_in(cla_2_c_out), .A(multiplexer_1_out[7:4]), .B(4'b0000), .sum(cla_1_sum));  // open: C_out
  CLA cla_2 (.C_in(bin[7]), .A(multiplexer_1_out[3:0]), .B(4'b0000), .C_out(cla_2_c_out), .sum({cla_2_sum, one[0]}));
  xor xor_4 (xor_4_out, 1'b0, and_4_out);
  xor xor_5 (xor_5_out, and_2_out, cla_1_sum[2]);
  or or_3 (or_3_out, xor_1_out, cla_1_sum[0]);
  and and_5 (and_5_out, xor_5_out, or_3_out);
  _7_Segment_Display u_7_segment_display_1 (.g(bin[7]));  // open: f, a, b, e, d, c, dp
  _7_Segment_Display u_7_segment_display_2 ();  // open: g, f, a, b, e, d, c, dp
  // BCD_to_7_Segment_decoder bcd_to_7_segment_decoder_1: pin names not known; wires that end beside it: {2'b00, hun[1:0]}
  or or_4 (or_4_out, xor_3_out, and_5_out);
  xor xor_6 (xor_6_out, or_4_out, cla_1_sum[0]);
  _7_Segment_Display u_7_segment_display_3 ();  // open: g, f, a, b, e, d, c, dp
  // BCD_to_7_Segment_decoder bcd_to_7_segment_decoder_2: pin names not known; wires that end beside it: ten
  not not_3 (not_3_out, xor_1_out);
  and and_6 (and_6_out, or_4_out, xor_6_out);
  _7_Segment_Display u_7_segment_display_4 ();  // open: g, f, a, b, e, d, c, dp
  // BCD_to_7_Segment_decoder bcd_to_7_segment_decoder_3: pin names not known; wires that end beside it: one
  xor xor_7 (xor_7_out, or_4_out, and_7_out);
  and and_7 (and_7_out, not_3_out, and_6_out);
  and and_8 (and_8_out, xor_5_out, xor_7_out);
  xor xor_8 (xor_8_out, xor_7_out, xor_5_out);
  xor xor_9 (xor_9_out, xor_3_out, and_8_out);
  xor xor_10 (xor_10_out, and_6_out, xor_1_out);
  and and_9 (and_9_out, xor_10_out, or_5_out);
  or or_5 (or_5_out, xor_6_out, cla_2_sum[3]);
  or or_6 (or_6_out, xor_8_out, and_9_out);
  not not_4 (not_4_out, xor_6_out);
  and and_10 (and_10_out, or_6_out, xor_11_out);
  xor xor_11 (xor_11_out, or_6_out, cla_2_sum[3]);
  and and_11 (and_11_out, not_4_out, and_10_out);
  and and_12 (and_12_out, xor_10_out, xor_12_out);
  xor xor_12 (xor_12_out, or_6_out, and_11_out);
  xor xor_13 (xor_13_out, xor_8_out, and_12_out);
  xor xor_14 (xor_14_out, xor_12_out, xor_10_out);
  xor xor_15 (xor_15_out, and_10_out, xor_6_out);
  or or_7 (or_7_out, xor_9_out, xor_13_out);
  or or_8 (or_8_out, xor_11_out, cla_2_sum[2]);
  or or_9 (or_9_out, 1'b0, and_13_out);
  and and_13 (and_13_out, xor_4_out, or_7_out);
  or or_10 (or_10_out, xor_14_out, and_14_out);
  and and_14 (and_14_out, xor_15_out, or_8_out);
  xor xor_16 (xor_16_out, or_9_out, xor_13_out);
  xor xor_17 (xor_17_out, or_10_out, cla_2_sum[2]);
  not not_5 (not_5_out, xor_9_out);
  and and_15 (and_15_out, not_5_out, and_16_out);
  and and_16 (and_16_out, or_9_out, xor_16_out);
  not not_6 (not_6_out, xor_11_out);
  and and_17 (and_17_out, not_6_out, and_18_out);
  and and_18 (and_18_out, or_10_out, xor_17_out);
  xor xor_18 (xor_18_out, or_9_out, and_15_out);
  xor xor_19 (xor_19_out, or_10_out, and_17_out);
  xor xor_20 (hun[1], 1'b0, and_19_out);
  and and_19 (and_19_out, xor_4_out, xor_18_out);
  xor xor_21 (xor_21_out, xor_18_out, xor_4_out);
  buf xor_22 (xor_22_out, xor_9_out);  // XOR_Gate
  xor xor_23 (xor_23_out, xor_14_out, and_20_out);
  and and_20 (and_20_out, xor_15_out, xor_19_out);
  xor xor_24 (xor_24_out, xor_19_out, xor_15_out);
  xor xor_25 (xor_25_out, and_18_out, xor_11_out);
  or or_11 (or_11_out, xor_16_out, xor_23_out);
  or or_12 (or_12_out, xor_17_out, cla_2_sum[1]);
  or or_13 (or_13_out, xor_21_out, and_21_out);
  and and_21 (and_21_out, xor_22_out, or_11_out);
  or or_14 (or_14_out, xor_24_out, and_22_out);
  and and_22 (and_22_out, xor_25_out, or_12_out);
  xor xor_26 (ten[1], or_13_out, xor_23_out);
  xor xor_27 (one[1], or_14_out, cla_2_sum[1]);
  not not_7 (not_7_out, xor_16_out);
  and and_23 (and_23_out, or_13_out, ten[1]);
  not not_8 (not_8_out, xor_17_out);
  and and_24 (and_24_out, or_14_out, one[1]);
  xor xor_28 (xor_28_out, or_13_out, and_25_out);
  and and_25 (and_25_out, not_7_out, and_23_out);
  xor xor_29 (xor_29_out, or_14_out, and_26_out);
  and and_26 (and_26_out, not_8_out, and_24_out);
  and and_27 (and_27_out, xor_22_out, xor_28_out);
  xor xor_30 (ten[3], xor_28_out, xor_22_out);
  and and_28 (and_28_out, xor_25_out, xor_29_out);
  xor xor_31 (one[3], xor_29_out, xor_25_out);
  xor xor_32 (hun[0], xor_21_out, and_27_out);
  xor xor_33 (ten[2], and_23_out, xor_16_out);
  xor xor_34 (ten[0], xor_24_out, and_28_out);
  xor xor_35 (one[2], and_24_out, xor_17_out);

  assign hun[3:2] = 2'b00;
  assign sign = bin[7];
endmodule
